// Logisim project Checkpoint2.circ as structural Verilog: 5 circuits, main circuit MemoryBit
module MemoryBit (
  input  W,
  input  D,
  input  Y,
  input  X,
  output Out
);

  wire and_1_out, and_2_out, d_ff_1_q;

  and and_1 (and_1_out, Y, X);
  and and_2 (and_2_out, W, and_1_out);
  D_Flip_Flop d_ff_1 (.clk(and_2_out), .D(D), .Q(d_ff_1_q));  // open: Qn, preset, en, reset
  and and_3 (Out, d_ff_1_q, and_1_out);
endmodule

module Memory (
  input  [1:0] Y,
  input  [1:0] X,
  input  D,
  input  W,
  input  R,
  output DataOut
);

  wire decoder_1_out0, decoder_1_out1, decoder_1_out2, decoder_1_out3, decoder_2_out0, decoder_2_out1,
       decoder_2_out2, decoder_2_out3, memorybit_1_out, memorybit_2_out, memorybit_3_out, memorybit_4_out,
       memorybit_5_out, memorybit_6_out, memorybit_7_out, memorybit_8_out, memorybit_9_out, memorybit_10_out,
       memorybit_11_out, memorybit_12_out, memorybit_13_out, memorybit_14_out, memorybit_15_out,
       memorybit_16_out, or_1_out, or_2_out, or_3_out, or_4_out, or_5_out;

  Decoder #(.select(2), .enable("false")) decoder_1 (
    .out0(decoder_1_out0), .out1(decoder_1_out1), .out2(decoder_1_out2), .out3(decoder_1_out3), .sel(X));
  MemoryBit memorybit_1 (.Y(decoder_2_out0), .X(decoder_1_out0), .Out(memorybit_1_out), .W(W), .D(D));
  MemoryBit memorybit_2 (.Y(decoder_2_out0), .X(decoder_1_out1), .Out(memorybit_2_out), .W(W), .D(D));
  MemoryBit memorybit_3 (.Y(decoder_2_out0), .X(decoder_1_out2), .Out(memorybit_3_out), .W(W), .D(D));
  MemoryBit memorybit_4 (.Y(decoder_2_out0), .X(decoder_1_out3), .Out(memorybit_4_out), .W(W), .D(D));
  Decoder #(.select(2), .enable("false")) decoder_2 (
    .out0(decoder_2_out0), .out1(decoder_2_out1), .out2(decoder_2_out2), .out3(decoder_2_out3), .sel(Y));
  or or_1 (or_1_out, memorybit_4_out, memorybit_3_out, memorybit_2_out, memorybit_1_out);
  MemoryBit memorybit_5 (.Y(decoder_2_out1), .X(decoder_1_out0), .Out(memorybit_5_out), .W(W), .D(D));
  MemoryBit memorybit_6 (.Y(decoder_2_out1), .X(decoder_1_out1), .Out(memorybit_6_out), .W(W), .D(D));
  MemoryBit memorybit_7 (.Y(decoder_2_out1), .X(decoder_1_out2), .Out(memorybit_7_out), .W(W), .D(D));
  MemoryBit memorybit_8 (.Y(decoder_2_out1), .X(decoder_1_out3), .Out(memorybit_8_out), .W(W), .D(D));
  or or_2 (or_2_out, memorybit_8_out, memorybit_7_out, memorybit_6_out, memorybit_5_out);
  MemoryBit memorybit_9 (.Y(decoder_2_out2), .X(decoder_1_out0), .Out(memorybit_9_out), .W(W), .D(D));
  MemoryBit memorybit_10 (.Y(decoder_2_out2), .X(decoder_1_out1), .Out(memorybit_10_out), .W(W), .D(D));
  MemoryBit memorybit_11 (.Y(decoder_2_out2), .X(decoder_1_out2), .Out(memorybit_11_out), .W(W), .D(D));
  MemoryBit memorybit_12 (.Y(decoder_2_out2), .X(decoder_1_out3), .Out(memorybit_12_out), .W(W), .D(D));
  or or_3 (or_3_out, memorybit_12_out, memorybit_11_out, memorybit_10_out, memorybit_9_out);
  MemoryBit memorybit_13 (.Y(decoder_2_out3), .X(decoder_1_out0), .Out(memorybit_13_out), .W(W), .D(D));
  MemoryBit memorybit_14 (.Y(decoder_2_out3), .X(decoder_1_out1), .Out(memorybit_14_out), .W(W), .D(D));
  MemoryBit memorybit_15 (.Y(decoder_2_out3), .X(decoder_1_out2), .Out(memorybit_15_out), .W(W), .D(D));
  MemoryBit memorybit_16 (.Y(decoder_2_out3), .X(decoder_1_out3), .Out(memorybit_16_out), .W(W), .D(D));
  and and_1 (DataOut, R, or_5_out);
  or or_4 (or_4_out, memorybit_16_out, memorybit_15_out, memorybit_14_out, memorybit_13_out);
  or or_5 (or_5_out, or_4_out, or_3_out, or_2_out, or_1_out);
endmodule

module Ula (
  input  Carry_In,
  input  [1:0] R0,
  input  [1:0] R1,
  input  A0,
  input  B0,
  input  A1,
  input  B1,
  output Out0,
  output Out1,
  output Carry_Out
);

  wire and_1_out, and_2_out, and_3_out, and_4_out, and_5_out, and_6_out, nor_1_out, nor_2_out, nor_3_out,
       nor_4_out, nor_5_out, nor_6_out, or_1_out, or_2_out, or_3_out;

  nor nor_1 (nor_1_out, A0, B0);
  and and_1 (and_1_out, A0, B0);
  or or_1 (or_1_out, A0, B0);
  nor nor_2 (nor_2_out, A0, B0);
  nor nor_3 (nor_3_out, A1, B1);
  and and_2 (and_2_out, A1, B1);
  or or_2 (or_2_out, A1, B1);
  nor nor_4 (nor_4_out, A1, B1);
  nor nor_5 (nor_5_out, nor_2_out, Carry_In);
  and and_3 (and_3_out, Carry_In, nor_2_out);
  and and_4 (and_4_out, A0, B0);
  nor nor_6 (nor_6_out, nor_4_out, or_3_out);
  and and_5 (and_5_out, or_3_out, nor_4_out);
  and and_6 (and_6_out, A1, B1);
  or or_3 (or_3_out, and_3_out, and_4_out);
  or or_4 (Carry_Out, and_5_out, and_6_out);
  Multiplexer #(.select(2), .enable("false")) multiplexer_1 (
    .in0(nor_1_out), .in1(and_1_out), .in2(or_1_out), .in3(nor_5_out), .out(Out0), .sel(R0));
  Multiplexer #(.select(2), .enable("false")) multiplexer_2 (
    .in0(nor_3_out), .in1(and_2_out), .in2(or_2_out), .in3(nor_6_out), .out(Out1), .sel(R1));
endmodule

module Geral (
  input  R,
  input  W,
  input  [1:0] X,
  input  [1:0] Y,
  input  CarryIn,
  input  [1:0] R0,
  input  [1:0] R1,
  input  CS,
  input  CS_2,
  output CarryOut
);

  wire buffer_1_out0, buffer_1_out1, buffer_2_out0, buffer_2_out1, buffer_3_out0, buffer_3_out1,
       memory_1_dataout, memory_2_dataout, not_1_out, ula_1_out0, ula_1_out1;

  Memory memory_1 (.Y(Y), .X(X), .D(buffer_3_out0), .W(W), .R(R), .DataOut(memory_1_dataout));
  Memory memory_2 (.Y(Y), .X(X), .D(buffer_3_out1), .W(W), .R(R), .DataOut(memory_2_dataout));
  Buffer buffer_1 (
    .Y(CS), .W(W), .D0(memory_2_dataout), .D1(memory_1_dataout), .Out0(buffer_1_out0), .out1(buffer_1_out1));
  Buffer buffer_2 (
    .Y(CS_2), .W(W), .D0(memory_2_dataout), .D1(memory_1_dataout), .Out0(buffer_2_out0), .out1(buffer_2_out1));
  not not_1 (not_1_out, CarryOut);
  Ula ula_1 (
    .A0(buffer_1_out0), .B0(buffer_1_out1), .A1(buffer_2_out0), .B1(buffer_2_out1), .Carry_In(CarryIn),
    .R0(R0), .R1(R1), .Out0(ula_1_out0), .Out1(ula_1_out1), .Carry_Out(CarryOut));
  Buffer buffer_3 (.Y(not_1_out), .W(W), .D0(ula_1_out0), .D1(ula_1_out1), .Out0(buffer_3_out0), .out1(buffer_3_out1));
endmodule

module Buffer (
  input  Y,
  input  W,
  input  D0,
  input  D1,
  output Out0,
  output out1
);

  MemoryBit memorybit_1 (.Y(Y), .X(Y), .Out(out1), .W(W), .D(D0));
  MemoryBit memorybit_2 (.Y(Y), .X(Y), .Out(Out0), .W(W), .D(D1));
endmodule
